# Fritzing sketch EX 6-4 電路圖  (saved by Fritzing 0.7.11b)
breadboards: 1

parts:
  元件1 = Thumb Joystick
  LED1 = RGB LED (com. cathode, rgb) [package="5 mm [THT]"]
  U1 = Arduino Mega

nets:
  GND: 元件1.GND, LED1.common_cathode, U1.GND
  N1: 元件1.SEL, U1.D13
  N2: 元件1.HORZ, U1.A3
  N3: 元件1.VERT, U1.A2
  VCC: 元件1.VCC, U1.VIN
  N4: LED1.red_anode, U1.D6
  N5: LED1.green_anode, U1.D5
  N6: LED1.blue_anode, U1.D3
