# Fritzing sketch EX 10-1 電路圖  (saved by Fritzing 0.7.11b)
breadboards: 1

parts:
  U1 = Arduino Mega
  U2 = XBee
  M1 = DC Motor
  M2 = DC Motor
  M3 = DC Motor
  R2 = Temperature Sensor (Thermistor) [thermistor_type=NTC package=THT]

nets:
  N1: U1.D6, M1.pin_1
  N2: U1.D5, M3.pin_1
  N3: U1.D3, M2.pin_1
  N4: U1.D1TX, U2.pin2
  N5: U1.D0RX, U2.pin3
  3V3: U1.3V3, U2.VCC
  GND: U1.GND, U2.GND, M1.pin_2, M2.pin_2, M3.pin_2, R2.pin_1
  N6: U1.A1, R2.pin_0

notes:
  發熱片
