# Fritzing sketch EX 12-1 電路圖 (saved by Fritzing 0.7.11b)
breadboards: 1

parts:
  U1 = Arduino Mega
  J1 = Basic Servo
  J2 = Basic Servo

nets:
  GND: U1.GND, J1.gnd, J2.gnd
  N1: U1.D7, J1.pulse
  N2: U1.D6, J2.pulse
  VCC: U1.+5V, J1.vcc, J2.vcc
